// Logisim project 4.4) Incrémenteur-décrémenteur.circ as structural Verilog: 1 circuit, main circuit main
module main (
  output [3:0] out_1
);

  wire clock_1_out, comparator_1_eq, comparator_2_eq, d_ff_1_q, not_1_out, or_1_out;
  wire [3:0] adder_1_out, multiplexer_1_out, subtractor_1_out;

  Clock clock_1 (.out(clock_1_out));
  Adder #(.width(4)) adder_1 (.a(out_1), .b(4'b0001), .out(adder_1_out));  // open: cin, cout
  Register #(.width(4)) register_1 (.D(multiplexer_1_out), .Q(out_1), .clk(clock_1_out));  // open: en, clr
  Multiplexer #(.width(4)) multiplexer_1 (
    .in0(adder_1_out), .in1(subtractor_1_out), .out(multiplexer_1_out), .sel(d_ff_1_q));  // open: en
  Subtractor #(.width(4)) subtractor_1 (.a(adder_1_out), .b(4'b0010), .out(subtractor_1_out));  // open: bin, bout
  or or_1 (or_1_out, comparator_1_eq, comparator_2_eq);
  Comparator #(.width(4), .mode("unsigned")) comparator_1 (
    .a(4'b0000), .b(out_1), .eq(comparator_1_eq));  // open: gt, lt
  Comparator #(.width(4), .mode("unsigned")) comparator_2 (
    .a(out_1), .b(4'b1111), .eq(comparator_2_eq));  // open: gt, lt
  not not_1 (not_1_out, d_ff_1_q);
  D_Flip_Flop d_ff_1 (.clk(or_1_out), .D(not_1_out), .Q(d_ff_1_q));  // open: Qn, preset, en, reset
endmodule
